# Fritzing sketch Fritzing File (saved by Fritzing 0.9.3b)
breadboards: 1

parts:
  Part1 = Arduino Uno (Rev3)
  Max1 = chipKIT Max32 [chip_label=IC package="SIP (Single Inline) [THT]"]
  Part3 = XBee USB Mini Adapter  # not connected
  M1 = cytron XBee shield
  Raspberry_Pi_1 = Raspberry Pi 3 [part_number=RPI-3-V1.2]  # not connected
  U1 = XBEE-1 [package=xbee-silk]  # not connected
  U2 = XBEE-1 [package=xbee-silk]  # not connected
  USBTTL1 = Micro USB B Plug
  USBTTL2 = USB A Plug
  J1 = Infrared Proximity Sensor
  HC-SR04_Sensor_1 = HC-SR04 Ultrasonic Distance Sensor
  LED1 = RGB LED (com. cathode, rbg) [package="5 mm [THT]"]
  HC-SR04_Sensor_2 = HC-SR04 Ultrasonic Distance Sensor
  HC-SR04_Sensor_3 = HC-SR04 Ultrasonic Distance Sensor
  LED2 = RGB LED (com. cathode, rbg) [package="5 mm [THT]"]
  LED3 = RGB LED (com. cathode, rbg) [package="5 mm [THT]"]
  J2 = Infrared Proximity Sensor
  J3 = Infrared Proximity Sensor
  16-Channel_Servo_Controller1 = 16-Channel Servo Controller [part_number="16-Channel Servo Controller" package="DIP (Dual Inline) [THT]"]
  M2 = Dagu DGServo 9g (Top view) [part_number=RS001B]
  M3 = Dagu DGServo 9g (Top view) [part_number=RS001B]
  M4 = Dagu DGServo 9g (Top view) [part_number=RS001B]

nets:
  N1: Part1.A0, M1.A0
  N2: Part1.A1, M1.A1
  N3: Part1.A2, M1.A2
  N4: Part1.A3, M1.A3
  N5: Part1.A4/SDA, M1.A4
  N6: Part1.A5/SCL, M1.A5
  N7: Part1.D8, M1.D8
  N8: Part1.D9_PWM, M1.~D9
  N9: Part1.D10_PWM/SS, M1.~D10
  N10: Part1.D11_PWM/MOSI, M1.~D11
  N11: Part1.D12/MISO, M1.D12
  N12: Part1.D13/SCK, M1.D13
  GND: Part1.GND, M1.GND, J1.GND, HC-SR04_Sensor_1.GND, LED1.common_cathode, HC-SR04_Sensor_2.GND, HC-SR04_Sensor_3.GND, LED2.common_cathode, LED3.common_cathode, J2.GND, J3.GND, 16-Channel_Servo_Controller1.GND#3
  N13: Part1.AREF, M1.AREF
  N14: Part1.D0/RX, M1.RX0/D0
  N15: Part1.D1/TX, M1.TX0/D1
  N16: Part1.D2, M1.D2
  N17: Part1.D3_PWM, Max1.D0, M1.~D3
  N18: Part1.D4, M1.D4
  N19: Part1.D5_PWM, M1.~D5
  N20: Part1.D6_PWM, M1.~D6
  N21: Part1.D7, M1.D7
  N22: Part1.RESET, M1.RESET
  3V3: Part1.3V3, M1.3V3
  VCC: Part1.5V, Max1.5V, M1.5V, J1.Vcc, HC-SR04_Sensor_1.VCC, HC-SR04_Sensor_2.VCC, HC-SR04_Sensor_3.VCC, J2.Vcc, J3.Vcc, 16-Channel_Servo_Controller1.+3v3
  VIN: Part1.VIN, M1.VIN
  N23: Max1.D25, J1.Vout
  N24: Max1.D27, J2.Vout
  N25: Max1.D29, J3.Vout
  N26: Max1.D36, HC-SR04_Sensor_3.TRIG
  N27: Max1.D37, HC-SR04_Sensor_3.ECHO
  N28: Max1.D40, HC-SR04_Sensor_1.TRIG
  N29: Max1.D41, HC-SR04_Sensor_1.ECHO
  N30: Max1.D44, HC-SR04_Sensor_2.TRIG
  N31: Max1.D45, HC-SR04_Sensor_2.ECHO
  N32: Max1.D52, 16-Channel_Servo_Controller1.RX
  N33: Max1.D70, LED1.green_anode
  N34: Max1.D71, LED1.blue_anode
  N35: Max1.D72, LED1.red_anode
  N36: Max1.D73, LED3.green_anode
  N37: Max1.D74, LED3.blue_anode
  N38: Max1.D75, LED3.red_anode
  N39: Max1.D76, LED2.green_anode
  N40: Max1.D77, LED2.blue_anode
  N41: Max1.D78, LED2.red_anode
  N42: USBTTL1.usb, USBTTL2.usb
  N43: 16-Channel_Servo_Controller1.S0, M4.pulse
  N44: 16-Channel_Servo_Controller1.VCC#7, M4.vcc
  N45: 16-Channel_Servo_Controller1.GND#8, 16-Channel_Servo_Controller1.GND#11, M4.gnd
  N46: 16-Channel_Servo_Controller1.S3, M3.pulse
  N47: 16-Channel_Servo_Controller1.VCC#16, 16-Channel_Servo_Controller1.VCC#22, M3.vcc
  N48: 16-Channel_Servo_Controller1.GND#17, M3.gnd
  N49: 16-Channel_Servo_Controller1.S6, M2.pulse
  N50: 16-Channel_Servo_Controller1.VCC#25, M2.vcc
  N51: 16-Channel_Servo_Controller1.GND#26, M2.gnd

custom parts:
  chipKIT Max32: chipKIT's Max32
  cytron XBee shield: .This is the newly designed XBee Shield. It comes WITHOUT XBee module offering freedom to choose which ever compatible Xbee module you like to use :) It is a XBee expansion board that design for Arduino and you need to buy a XBee module separately.
  16-Channel Servo Controller: Independent control of up to 16 RC servo motor in a single board. 1uS pulse width resolution. Serial TTL level UART I/O port interfaces easily with most microcontrollers, including gizDuino (Arduino Compatible Board). Easy to use command set. Additional Power Modules : Servo Soft Starter
